// Logisim project Comparadores.circ as structural Verilog
module igualdad (
  input  [4:0] A,
  input  [4:0] B,
  output out_3
);

  wire xnor_1_out, xnor_2_out, xnor_3_out, xnor_4_out, xnor_5_out;

  xnor xnor_1 (xnor_1_out, A[0], B[0]);
  xnor xnor_2 (xnor_2_out, A[1], B[1]);
  xnor xnor_3 (xnor_3_out, A[2], B[2]);
  xnor xnor_4 (xnor_4_out, A[3], B[3]);
  xnor xnor_5 (xnor_5_out, A[4], B[4]);
  and and_1 (out_3, xnor_1_out, xnor_2_out, xnor_3_out, xnor_4_out, xnor_5_out);

  // Other names for the same wires on the sheet: a1 = A[0]; a2 = A[1]; a3 = A[2]; a4 = A[3]; a5 = A[4]; b1 = B[0];
  //   b2 = B[1]; b3 = B[2]; b4 = B[3]; b5 = B[4]

  // Notes on the sheet:
  //   A
  //   B
endmodule

module mayor (
  input  [4:0] A,
  input  [4:0] B,
  output mayor
);

  wire a1andnb1, a2andnb2, a3andnb3, a4andnb4, a5andnb5, bit1, bit2, bit3, bit4;

  and and_1 (a5andnb5, A[4], ~B[4]);  // AND_Gate
  and and_2 (a4andnb4, A[3], ~B[3]);  // AND_Gate
  and and_3 (a3andnb3, A[2], ~B[2]);  // AND_Gate
  and and_4 (a2andnb2, A[1], ~B[1]);  // AND_Gate
  and and_5 (a1andnb1, A[0], ~B[0]);  // AND_Gate
  and and_6 (bit4, a4andnb4, ~B[4]);  // AND_Gate
  and and_7 (bit3, a3andnb3, ~B[3], ~B[4]);  // AND_Gate
  and and_8 (bit2, a2andnb2, ~B[2], ~B[3], ~B[4]);  // AND_Gate
  and and_9 (bit1, a1andnb1, ~B[1], ~B[2], ~B[3], ~B[4]);  // AND_Gate
  ExactlyOne xor_1 (.out(mayor), .in0(bit1), .in1(bit2), .in2(bit3), .in3(bit4), .in4(a5andnb5));

  // Other names for the same wires on the sheet: a1 = A[0]; a2 = A[1]; a3 = A[2]; a4 = A[3]; a5 = A[4]; b1 = B[0];
  //   b2 = B[1]; b3 = B[2]; b4 = B[3]; b5 = B[4]

  // Notes on the sheet:
  //   A
  //   B
endmodule

module comparador (
  input  [4:0] A,
  input  [4:0] B,
  output out_3,
  output out_4,
  output out_5
);

  mayor mayor_1 (.A(A), .B(B), .mayor(out_3));
  igualdad igualdad_1 (.A(A), .B(B), .out_3(out_4));
  mayor mayor_2 (.A(B), .B(A), .mayor(out_5));
endmodule
